# Fritzing sketch sensor_schematic (saved by Fritzing 0.9.4)
breadboards: 1

parts:
  U1 = ESP32S-HiLetgo [part_number=ESP32S-HiLetgo]
  R1_4_7K = Resistor [tolerance=±5% resistance=220 package=THT]
  R2_4_7K = Resistor [tolerance=±5% resistance=220 package=THT]
  part = Adafruit BME680

nets:
  N1: U1.3.3, R1_4_7K.Pin_1, R2_4_7K.Pin_1, part.3.3V
  GND: U1.GND, part.GND
  N2: U1.GPIO21, R2_4_7K.Pin_0, part.SDO/ADR
  N3: U1.GPIO22, R1_4_7K.Pin_0, part.SCK/SCL

custom parts:
  ESP32S-HiLetgo: HiLetgo ESP-WROOM-32 ESP32 ESP-32S Development Board 2.4GHz Dual-Mode WiFi + Bluetooth Dual Cores Microcontroller The ESP32 integrated with Antenna switches, RF Balun, power amplifiers, low-noise amplifiers, filters, and management modules, and the entire solution occupies the least area of PCB. 2.4 GHz Wi-Fi plus Bluetooth dual-mode chip, with TSMC Ultra-low power consumption 40nm technology,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
